# Fritzing sketch Triac (Lamp dimmer) (saved by Fritzing 0.7.4b)
perfboards: 1

parts:
  LOAD = Screw terminal - 2 pins [package=THT]
  220 = Screw terminal - 2 pins [package=THT]
  R1 = Resistor [tolerance=±5% resistance=220 package=THT]
  MOC3061 = Optocoupler [package=THT]
  R2 = Resistor [tolerance=±5% resistance=470 package=THT]
  GND = female pin header, 2 pins [form="♀ (female)"]
  BT137 = BTA Triac [part_number=BT137 package="TO220 [THT]"]

nets:
  N1: LOAD.pin1, R1.Pin_0, BT137.A2
  N2: LOAD.pin2, 220.pin1
  N3: 220.pin2, BT137.A1
  N4: R1.Pin_1, MOC3061.Pin_6
  GND: MOC3061.Pin_2, GND.pin1
  N5: MOC3061.Pin_4, BT137.G
  N6: R2.Pin_1, GND.pin2

notes:
  PWM

custom parts:
  Optocoupler: Optoisolator Zero-Cross Triac Driver
  BTA Triac: BTA16
